// Logisim project S3S2S1S0ZCin_using_74138.circ as structural Verilog: 1 circuit, main circuit main
module main (
  input  cs2,
  input  cs1,
  input  cs0,
  output S3,
  output S2,
  output S1,
  output S0,
  output Cin,
  output Z
);

  wire n7404_1__6__3y, n7408_1__3__1y, n74138_1__7__y7, n74138_1__9__y6, n74138_1__11__y4, n74138_1__12__y3,
       n74138_1__14__y1;

  _7404 u_7404_1 (
    ._5__3A(n74138_1__11__y4), ._6__3Y(n7404_1__6__3y), ._7__GND(1'b0), ._14__Vcc(1'b1),
    ._9__4A(n74138_1__12__y3), ._8__4Y(S3));  // open: _1__1A, _2__1Y, _3__2A, _4__2Y, _13__6A, _12__6Y, _11__5A, _10__5Y
  _7432 u_7432_1 (
    ._7__GND(1'b0), ._14__Vcc(1'b1), ._13__4B(n7404_1__6__3y), ._12__4A(S3), ._11__4Y(Cin));  // open: _1__1A, _2__1B, _3__1Y, _4__2A, _5__2B, _6__2Y, _10__3B, _9__3A, _8__3Y
  _74138 u_74138_1 (
    ._1__A(cs0), ._2__B(cs1), ._3__C(cs2), ._4__G2A(1'b0), ._5__G2B(1'b0), ._6__G1(1'b1),
    ._7__Y7(n74138_1__7__y7), ._8__GND(1'b0), ._16__Vcc(1'b1), ._14__Y1(n74138_1__14__y1),
    ._12__Y3(n74138_1__12__y3), ._11__Y4(n74138_1__11__y4), ._10__Y5(S1), ._9__Y6(n74138_1__9__y6));  // open: _15__Y0, _13__Y2
  _7408 u_7408_1 (
    ._1__1A(S1), ._2__1B(n74138_1__9__y6), ._3__1Y(n7408_1__3__1y), ._4__2A(n7408_1__3__1y),
    ._5__2B(n74138_1__7__y7), ._6__2Y(S0), ._7__GND(1'b0), ._14__Vcc(1'b1), ._13__4B(n74138_1__11__y4),
    ._12__4A(n74138_1__14__y1), ._11__4Y(S2), ._10__3B(n74138_1__12__y3), ._9__3A(S0), ._8__3Y(Z));
endmodule
