// Logisim project final ALU.circ as structural Verilog: 1 circuit, main circuit main
module main (
  input  A3,
  input  A2,
  input  A1,
  input  A0,
  input  B3,
  input  B2,
  input  B1,
  input  B0,
  input  cs2,
  input  cs1,
  input  cs0,
  output Cout,
  output O3,
  output O2,
  output O1,
  output O0,
  output C,
  output S,
  output V,
  output Z
);

  wire ic_7483_1__2__s3, ic_7483_1__6__s2, ic_7483_1__9__s1, ic_7483_1__15__s4, n7404_1__2__1y,
       n7404_1__4__2y, n7404_1__6__3y, n7404_1__8__4y, n7404_1__10__5y, n7404_1__12__6y, n7408_1__3__1y,
       n7408_1__6__2y, n7408_1__8__3y, n7408_1__11__4y, n7408_2__3__1y, n7408_2__6__2y, n7408_2__8__3y,
       n7408_2__11__4y, n7432_1__3__1y, n7432_1__6__2y, n7432_1__8__3y, n7432_1__11__4y, n7486_1__3__1y,
       n7486_1__6__2y, n7486_1__8__3y, n7486_1__11__4y, n7486_2__3__1y, n7486_2__6__2y, n7486_2__8__3y,
       n7486_2__11__4y, n7486_3__3__1y, n7486_3__11__4y, n74138_1__7__y7, n74138_1__9__y6, n74138_1__10__y5,
       n74138_1__11__y4, n74138_1__12__y3, n74138_1__14__y1, n74157_1__4__y1, n74157_1__7__y2,
       n74157_1__9__y3, n74157_1__12__y4, n74157_3__4__y1, n74157_3__7__y2, n74157_3__9__y3, n74157_3__12__y4;

  _7408 u_7408_1 (
    ._1__1A(A0), ._2__1B(B0), ._3__1Y(n7408_1__3__1y), ._4__2A(A1), ._5__2B(B1), ._6__2Y(n7408_1__6__2y),
    ._7__GND(1'b0), ._14__Vcc(1'b1), ._13__4B(B3), ._12__4A(A3), ._11__4Y(n7408_1__11__4y), ._10__3B(B2),
    ._9__3A(A2), ._8__3Y(n7408_1__8__3y));
  _74157 u_74157_1 (
    ._1__S(n74138_1__10__y5), ._2__A1(n7408_1__3__1y), ._3__B1(n7486_1__3__1y), ._4__Y1(n74157_1__4__y1),
    ._5__A2(n7408_1__6__2y), ._6__B2(n7486_1__6__2y), ._7__Y2(n74157_1__7__y2), ._8__GND(1'b0),
    ._16__Vcc(1'b1), ._15__G(1'b0), ._14__A4(n7408_1__11__4y), ._13__B4(n7486_1__11__4y),
    ._12__Y4(n74157_1__12__y4), ._11__A3(n7408_1__8__3y), ._10__B3(n7486_1__8__3y), ._9__Y3(n74157_1__9__y3));
  _7486 u_7486_1 (
    ._1__1A(A0), ._2__1B(B0), ._3__1Y(n7486_1__3__1y), ._4__2A(A1), ._5__2B(B1), ._6__2Y(n7486_1__6__2y),
    ._7__GND(1'b0), ._14__Vcc(1'b1), ._13__4B(B3), ._12__4A(A3), ._11__4Y(n7486_1__11__4y), ._10__3B(B2),
    ._9__3A(A2), ._8__3Y(n7486_1__8__3y));
  _74157 u_74157_2 (
    ._1__S(n7408_2__6__2y), ._2__A1(n74157_1__4__y1), ._3__B1(ic_7483_1__9__s1), ._4__Y1(O0),
    ._5__A2(n74157_1__7__y2), ._6__B2(ic_7483_1__6__s2), ._7__Y2(O1), ._8__GND(1'b0), ._16__Vcc(1'b1),
    ._15__G(1'b0), ._14__A4(n74157_1__12__y4), ._13__B4(ic_7483_1__15__s4), ._12__Y4(O3),
    ._11__A3(n74157_1__9__y3), ._10__B3(ic_7483_1__2__s3), ._9__Y3(O2));
  _7486 u_7486_2 (
    ._1__1A(A0), ._2__1B(n7404_1__8__4y), ._3__1Y(n7486_2__3__1y), ._4__2A(A1), ._5__2B(n7404_1__8__4y),
    ._6__2Y(n7486_2__6__2y), ._7__GND(1'b0), ._14__Vcc(1'b1), ._13__4B(n7404_1__8__4y), ._12__4A(A3),
    ._11__4Y(n7486_2__11__4y), ._10__3B(n7404_1__8__4y), ._9__3A(A2), ._8__3Y(n7486_2__8__3y));
  IC___7483 ic_7483_1 (
    ._1__A4(n7486_2__11__4y), ._2__S3(ic_7483_1__2__s3), ._3__A3(n7486_2__8__3y), ._4__B3(n74157_3__9__y3),
    ._5__Vcc(1'b1), ._6__S2(ic_7483_1__6__s2), ._7__B2(n74157_3__7__y2), ._8__A2(n7486_2__6__2y),
    ._16__B4(n74157_3__12__y4), ._15__S4(ic_7483_1__15__s4), ._14__Cout(C), ._13__Cin(n7432_1__11__4y),
    ._12__GND(1'b0), ._11__B1(n74157_3__4__y1), ._10__A1(n7486_2__3__1y), ._9__S1(ic_7483_1__9__s1));
  _7486 u_7486_3 (
    ._1__1A(n7486_2__11__4y), ._2__1B(n74157_3__12__y4), ._3__1Y(n7486_3__3__1y), ._4__2A(n7432_1__8__3y),
    ._5__2B(1'b1), ._6__2Y(Z), ._7__GND(1'b0), ._14__Vcc(1'b1), ._13__4B(C), ._12__4A(ic_7483_1__15__s4),
    ._11__4Y(n7486_3__11__4y), ._10__3B(n7486_3__11__4y), ._9__3A(n7486_3__3__1y), ._8__3Y(V));
  _7404 u_7404_1 (
    ._1__1A(B2), ._2__1Y(n7404_1__2__1y), ._3__2A(B3), ._4__2Y(n7404_1__4__2y), ._5__3A(n74138_1__11__y4),
    ._6__3Y(n7404_1__6__3y), ._7__GND(1'b0), ._14__Vcc(1'b1), ._13__6A(B1), ._12__6Y(n7404_1__12__6y),
    ._11__5A(B0), ._10__5Y(n7404_1__10__5y), ._9__4A(n74138_1__12__y3), ._8__4Y(n7404_1__8__4y));
  _74157 u_74157_3 (
    ._1__S(n7408_2__11__4y), ._2__A1(n7404_1__10__5y), ._3__B1(n7408_2__8__3y), ._4__Y1(n74157_3__4__y1),
    ._5__A2(n7404_1__12__6y), ._6__B2(n7408_2__8__3y), ._7__Y2(n74157_3__7__y2), ._8__GND(1'b0),
    ._16__Vcc(1'b1), ._15__G(1'b0), ._14__A4(n7404_1__4__2y), ._13__B4(n7408_2__8__3y),
    ._12__Y4(n74157_3__12__y4), ._11__A3(n7404_1__2__1y), ._10__B3(n7408_2__8__3y), ._9__Y3(n74157_3__9__y3));
  _7432 u_7432_1 (
    ._1__1A(O3), ._2__1B(O2), ._3__1Y(n7432_1__3__1y), ._4__2A(O1), ._5__2B(O0), ._6__2Y(n7432_1__6__2y),
    ._7__GND(1'b0), ._14__Vcc(1'b1), ._13__4B(n7404_1__6__3y), ._12__4A(n7404_1__8__4y),
    ._11__4Y(n7432_1__11__4y), ._10__3B(n7432_1__3__1y), ._9__3A(n7432_1__6__2y), ._8__3Y(n7432_1__8__3y));
  _74138 u_74138_1 (
    ._1__A(cs0), ._2__B(cs1), ._3__C(cs2), ._4__G2A(1'b0), ._5__G2B(1'b0), ._6__G1(1'b1),
    ._7__Y7(n74138_1__7__y7), ._8__GND(1'b0), ._16__Vcc(1'b1), ._14__Y1(n74138_1__14__y1),
    ._12__Y3(n74138_1__12__y3), ._11__Y4(n74138_1__11__y4), ._10__Y5(n74138_1__10__y5),
    ._9__Y6(n74138_1__9__y6));  // open: _15__Y0, _13__Y2
  _7408 u_7408_2 (
    ._1__1A(n74138_1__10__y5), ._2__1B(n74138_1__9__y6), ._3__1Y(n7408_2__3__1y), ._4__2A(n7408_2__3__1y),
    ._5__2B(n74138_1__7__y7), ._6__2Y(n7408_2__6__2y), ._7__GND(1'b0), ._14__Vcc(1'b1),
    ._13__4B(n74138_1__11__y4), ._12__4A(n74138_1__14__y1), ._11__4Y(n7408_2__11__4y),
    ._10__3B(n74138_1__12__y3), ._9__3A(n7408_2__6__2y), ._8__3Y(n7408_2__8__3y));

  assign Cout = C;
  assign S = O3;
endmodule
