// Logisim project 20to32bitExtenderWithMSBSet.circ as structural Verilog: 1 circuit, main circuit main
// 20->32BE
module main (
  output [31:0] _32_bit_output,
  output [19:0] _20_bit_input
);


  assign _32_bit_output = {1'b1, _20_bit_input, {11{1'b0}}};
endmodule
