// Logisim project 20to32bitExtractorWith21stBitSet.circ as structural Verilog: 1 circuit, main circuit main
// 20->32BE
module main (
  input  [19:0] _20_bit_input,
  output [31:0] _32_bit_output
);


  assign _32_bit_output = {1'b1, _20_bit_input, {11{1'b0}}};
endmodule
