// Logisim project 7400LibDefault.circ as structural Verilog: 2 circuits, main circuit main
module main (
);

  InputProcessor inputprocessor_1 ();  // open: A, B, ExponentA, ExponentB
endmodule

// InputProc
module InputProcessor (
  input  [31:0] A,
  input  [31:0] B,
  output [11:0] ExponentA,
  output [11:0] ExponentB
);


  assign ExponentA = {1'b0, A[30:20]};
  assign ExponentB = {1'b0, B[30:20]};

  // Other names for the same wires on the sheet: MantissaA[19:0] = A[19:0]; SignA = A[31]; MantissaB[19:0] = B[19:0];
  //   SignB = B[31]; ExpA[10:0] = A[30:20]; ExpB[10:0] = B[30:20]
endmodule
