// Logisim project Arbitrary right shifter.circ as structural Verilog: 1 circuit, main circuit main
// ARS
module main (
  input  [11:0] ExpDiff,
  input  [31:0] Significand,
  output [31:0] RightShiftOut
);

  wire n744075_1__6__2y, n744075_1__8__3y, n744075_1__12__1y;
  wire [31:0] shifter_1_out;

  _744075 u_744075_1 (
    ._1__1A(ExpDiff[7]), ._2__1B(ExpDiff[8]), ._3__2A(ExpDiff[5]), ._4__2B(ExpDiff[6]),
    ._5__2C(n744075_1__12__1y), ._6__2Y(n744075_1__6__2y), ._7__GND(1'b0), ._14__Vcc(1'b1),
    ._13__1C(n744075_1__8__3y), ._12__1Y(n744075_1__12__1y), ._11__3C(ExpDiff[11]), ._10__3B(ExpDiff[10]),
    ._9__3A(ExpDiff[9]), ._8__3Y(n744075_1__8__3y));
  Shifter #(.width(32), .shift("lr")) shifter_1 (.in(Significand), .\dist (ExpDiff[4:0]), .out(shifter_1_out));
  Multiplexer #(.width(32), .enable("false")) multiplexer_1 (
    .in0(shifter_1_out), .in1({32{1'b0}}), .out(RightShiftOut), .sel(n744075_1__6__2y));
endmodule
