// Logisim project ComplementerLib.circ as structural Verilog: 7 circuits, main circuit main
// CL
module main (
);

  _1sComplementer4bit u_1scomplementer4bit_1 ();  // open: Enable, _4bitInp, _4bitOut
  _2sComplementer4bit u_2scomplementer4bit_1 ();  // open: _4bitInp, Enable, Cout, _4bitOut
  _1sComplementer12bit u_1scomplementer12bit_1 ();  // open: Enable, _12bitInp, _12bitOut
  _2sComplementer12bit u_2scomplementer12bit_1 ();  // open: Enable, _12bitInp, _12bitOut, Cout
  _1sComplementer32bit u_1scomplementer32bit_1 ();  // open: Enable, _32bitInp, _32bitOut
  _2sComplementer32bit u_2scomplementer32bit_1 ();  // open: Enable, _32bitInp, _32bitOut, Cout
endmodule

// 1CL4
module _1sComplementer4bit (
  input  Enable,
  input  [3:0] _4bitInp,
  output [3:0] _4bitOut
);

  _7486 u_7486_1 (
    ._1__1A(_4bitInp[0]), ._2__1B(Enable), ._3__1Y(_4bitOut[0]), ._4__2A(_4bitInp[1]), ._5__2B(Enable),
    ._6__2Y(_4bitOut[1]), ._7__GND(1'b0), ._14__Vcc(1'b1), ._13__4B(_4bitInp[3]), ._12__4A(Enable),
    ._11__4Y(_4bitOut[3]), ._10__3B(_4bitInp[2]), ._9__3A(Enable), ._8__3Y(_4bitOut[2]));

  // Other names for the same wires on the sheet: EN = Enable
endmodule

// 1CL12
module _1sComplementer12bit (
  input  Enable,
  input  [11:0] _12bitInp,
  output [11:0] _12bitOut
);

  _1sComplementer4bit u_1scomplementer4bit_1 (.Enable(Enable), ._4bitInp(_12bitInp[3:0]), ._4bitOut(_12bitOut[3:0]));
  _1sComplementer4bit u_1scomplementer4bit_2 (.Enable(Enable), ._4bitInp(_12bitInp[7:4]), ._4bitOut(_12bitOut[7:4]));
  _1sComplementer4bit u_1scomplementer4bit_3 (.Enable(Enable), ._4bitInp(_12bitInp[11:8]), ._4bitOut(_12bitOut[11:8]));

  // Other names for the same wires on the sheet: _0_3A[3:0] = _12bitInp[3:0]; _4_7A[3:0] = _12bitInp[7:4];
  //   _8_11A[3:0] = _12bitInp[11:8]; _0_3Y[3:0] = _12bitOut[3:0]; _4_7Y[3:0] = _12bitOut[7:4];
  //   _8_11Y[3:0] = _12bitOut[11:8]; EN = Enable
endmodule

// 1CL32
module _1sComplementer32bit (
  input  Enable,
  input  [31:0] _32bitInp,
  output [31:0] _32bitOut
);

  _1sComplementer4bit u_1scomplementer4bit_1 (.Enable(Enable), ._4bitInp(_32bitInp[3:0]), ._4bitOut(_32bitOut[3:0]));
  _1sComplementer4bit u_1scomplementer4bit_2 (.Enable(Enable), ._4bitInp(_32bitInp[7:4]), ._4bitOut(_32bitOut[7:4]));
  _1sComplementer12bit u_1scomplementer12bit_1 (
    .Enable(Enable), ._12bitInp(_32bitInp[19:8]), ._12bitOut(_32bitOut[19:8]));
  _1sComplementer12bit u_1scomplementer12bit_2 (
    .Enable(Enable), ._12bitInp(_32bitInp[31:20]), ._12bitOut(_32bitOut[31:20]));

  // Other names for the same wires on the sheet: _0_3A[3:0] = _32bitInp[3:0]; _4_7A[3:0] = _32bitInp[7:4];
  //   _8_19A[11:0] = _32bitInp[19:8]; _20_31A[11:0] = _32bitInp[31:20]; _0_3Y[3:0] = _32bitOut[3:0];
  //   _4_7Y[3:0] = _32bitOut[7:4]; _8_19Y[11:0] = _32bitOut[19:8]; _20_31Y[11:0] = _32bitOut[31:20]; EN = Enable
endmodule

// 2CL4
module _2sComplementer4bit (
  input  [3:0] _4bitInp,
  input  Enable,
  output Cout,
  output [3:0] _4bitOut
);

  wire [3:0] n1scomplementer4bit_1__4bitout;

  _1sComplementer4bit u_1scomplementer4bit_1 (
    .Enable(Enable), ._4bitInp(_4bitInp), ._4bitOut(n1scomplementer4bit_1__4bitout));
  IC___7483 ic_7483_1 (
    ._1__A4(n1scomplementer4bit_1__4bitout[3]), ._2__S3(_4bitOut[2]),
    ._3__A3(n1scomplementer4bit_1__4bitout[2]), ._4__B3(1'b0), ._5__Vcc(1'b1), ._6__S2(_4bitOut[1]),
    ._7__B2(1'b0), ._8__A2(n1scomplementer4bit_1__4bitout[1]), ._16__B4(1'b0), ._15__S4(_4bitOut[3]),
    ._14__Cout(Cout), ._13__Cin(Enable), ._12__GND(1'b0), ._11__B1(1'b0),
    ._10__A1(n1scomplementer4bit_1__4bitout[0]), ._9__S1(_4bitOut[0]));

  // Other names for the same wires on the sheet: EN = Enable
endmodule

// 2CL12
module _2sComplementer12bit (
  input  Enable,
  input  [11:0] _12bitInp,
  output [11:0] _12bitOut,
  output Cout
);

  wire [11:0] n1scomplementer12bit_1__12bitout;

  _1sComplementer12bit u_1scomplementer12bit_1 (
    .Enable(Enable), ._12bitInp(_12bitInp), ._12bitOut(n1scomplementer12bit_1__12bitout));
  Adder #(.width(12)) adder_1 (
    .a(n1scomplementer12bit_1__12bitout), .b({12{1'b0}}), .out(_12bitOut), .cin(Enable), .cout(Cout));

  // Other names for the same wires on the sheet: EN = Enable
endmodule

// 2CL32
module _2sComplementer32bit (
  input  Enable,
  input  [31:0] _32bitInp,
  output [31:0] _32bitOut,
  output Cout
);

  wire [31:0] n1scomplementer32bit_1__32bitout;

  _1sComplementer32bit u_1scomplementer32bit_1 (
    .Enable(Enable), ._32bitInp(_32bitInp), ._32bitOut(n1scomplementer32bit_1__32bitout));
  Adder #(.width(32)) adder_1 (
    .a(n1scomplementer32bit_1__32bitout), .b({32{1'b0}}), .out(_32bitOut), .cin(Enable), .cout(Cout));

  // Other names for the same wires on the sheet: EN = Enable
endmodule
