// Logisim project ExponentProcessor.circ as structural Verilog: 2 circuits, main circuit main
// ExponentProcessor
module main (
  input  [11:0] ExponentA,
  input  [11:0] ExponentB,
  output Ea_Eb,
  output [11:0] ExpDiff
);

  wire [11:0] exponentcomparator_1_greaterexponent, exponentcomparator_1_lessexponent;

  exponentComparator exponentcomparator_1 (
    .ExponentA(ExponentA), .ExponentB(ExponentB), .GreaterExponent(exponentcomparator_1_greaterexponent),
    .lessExponent(exponentcomparator_1_lessexponent), .out_5(Ea_Eb));
  Subtractor #(.width(12)) subtractor_1 (
    .a(exponentcomparator_1_greaterexponent), .b(exponentcomparator_1_lessexponent), .out(ExpDiff), .bin(1'b0));  // open: bout
endmodule

// ExpComp
module exponentComparator (
  input  [11:0] ExponentA,
  input  [11:0] ExponentB,
  output [11:0] GreaterExponent,
  output [11:0] lessExponent,
  output out_5
);

  Comparator #(.width(12), .mode("unsigned")) comparator_1 (.a(ExponentA), .b(ExponentB), .lt(out_5));  // open: gt, eq
  Multiplexer #(.width(12)) multiplexer_1 (
    .in0(ExponentA), .in1(ExponentB), .out(GreaterExponent), .sel(out_5), .en(1'b1));
  Multiplexer #(.width(12)) multiplexer_2 (
    .in0(ExponentB), .in1(ExponentA), .out(lessExponent), .sel(out_5), .en(1'b1));
endmodule
