// Logisim project MantissaCentralProcessor.circ as structural Verilog: 3 circuits, main circuit main
// ManCentralProc
module main (
);

  _32BitInverterWithEnable u_32bitinverterwithenable_1 ();  // open: Enable, Input, Output
  MantissaCentralProcessor mantissacentralprocessor_1 ();  // open: ExpDiff, LargerExpSign, SmallerExpSign, SmallerExpMantissa, LargerExpMantissa, Sign_Y, C_out, Enable2sComplement, Adder_output
endmodule

// ManCentralProc
module MantissaCentralProcessor (
  input  [19:0] SmallerExpMantissa,
  input  [19:0] LargerExpMantissa,
  input  [11:0] ExpDiff,
  input  LargerExpSign,
  input  SmallerExpSign,
  output [31:0] Adder_output,
  output Enable2sComplement,
  output Sign_Y,
  output C_out
);

  wire n7408_1__3__1y, n7408_1__6__2y, n7486_1__3__1y, n7486_1__8__3y;
  wire [31:0] main_1__32_bit_output, main_2_rightshiftout, main_3__32_bit_output,
       n32bitinverterwithenable_1_output, n32bitinverterwithenable_2_output;

  _7486 u_7486_1 (
    ._1__1A(SmallerExpSign), ._2__1B(LargerExpSign), ._3__1Y(n7486_1__3__1y), ._7__GND(1'b0),
    ._14__Vcc(1'b1), ._10__3B(1'b1), ._9__3A(C_out), ._8__3Y(n7486_1__8__3y));  // open: _4__2A, _5__2B, _6__2Y, _13__4B, _12__4A, _11__4Y
  _7408 u_7408_1 (
    ._1__1A(n7486_1__3__1y), ._2__1B(LargerExpSign), ._3__1Y(n7408_1__3__1y), ._4__2A(n7486_1__3__1y),
    ._5__2B(SmallerExpSign), ._6__2Y(n7408_1__6__2y), ._7__GND(1'b0), ._14__Vcc(1'b1),
    ._10__3B(n7486_1__8__3y), ._9__3A(Sign_Y), ._8__3Y(Enable2sComplement));  // open: _13__4B, _12__4A, _11__4Y
  _20to32bitExtractorWith21stBitSet_main main_1 (
    ._20_bit_input(SmallerExpMantissa), ._32_bit_output(main_1__32_bit_output));
  Arbitrary_right_shifter_main main_2 (
    .Significand(main_1__32_bit_output), .RightShiftOut(main_2_rightshiftout), .ExpDiff(ExpDiff));
  _32BitInverterWithEnable u_32bitinverterwithenable_1 (
    .Enable(n7408_1__6__2y), .Input(main_2_rightshiftout), .Output(n32bitinverterwithenable_1_output));
  Multiplexer multiplexer_1 (
    .in0(SmallerExpSign), .in1(Adder_output[31]), .out(Sign_Y), .sel(n7486_1__3__1y), .en(1'b1));
  _20to32bitExtractorWith21stBitSet_main main_3 (
    ._20_bit_input(LargerExpMantissa), ._32_bit_output(main_3__32_bit_output));
  _32BitInverterWithEnable u_32bitinverterwithenable_2 (
    .Enable(n7408_1__3__1y), .Input(main_3__32_bit_output), .Output(n32bitinverterwithenable_2_output));
  Adder #(.width(32)) adder_1 (
    .a(n32bitinverterwithenable_2_output), .b(n32bitinverterwithenable_1_output), .out(Adder_output),
    .cin(n7486_1__3__1y), .cout(C_out));
endmodule

// 1CL32
module _32BitInverterWithEnable (
  input  Enable,
  input  [31:0] Input,
  output [31:0] Output
);

  // Probe on Enable
  _7486 u_7486_1 (
    ._1__1A(Input[0]), ._2__1B(Enable), ._3__1Y(Output[0]), ._4__2A(Input[1]), ._5__2B(Enable),
    ._6__2Y(Output[1]), ._7__GND(1'b0), ._14__Vcc(1'b1), ._13__4B(Input[2]), ._12__4A(Enable),
    ._11__4Y(Output[2]), ._10__3B(Input[3]), ._9__3A(Enable), ._8__3Y(Output[3]));
  _7486 u_7486_2 (
    ._1__1A(Input[4]), ._2__1B(Enable), ._3__1Y(Output[4]), ._4__2A(Input[5]), ._5__2B(Enable),
    ._6__2Y(Output[5]), ._7__GND(1'b0), ._14__Vcc(1'b1), ._13__4B(Input[6]), ._12__4A(Enable),
    ._11__4Y(Output[6]), ._10__3B(Input[7]), ._9__3A(Enable), ._8__3Y(Output[7]));
  _7486 u_7486_3 (
    ._1__1A(Input[8]), ._2__1B(Enable), ._3__1Y(Output[8]), ._4__2A(Input[9]), ._5__2B(Enable),
    ._6__2Y(Output[9]), ._7__GND(1'b0), ._14__Vcc(1'b1), ._13__4B(Input[10]), ._12__4A(Enable),
    ._11__4Y(Output[10]), ._10__3B(Input[11]), ._9__3A(Enable), ._8__3Y(Output[11]));
  _7486 u_7486_4 (
    ._1__1A(Input[12]), ._2__1B(Enable), ._3__1Y(Output[12]), ._4__2A(Input[13]), ._5__2B(Enable),
    ._6__2Y(Output[13]), ._7__GND(1'b0), ._14__Vcc(1'b1), ._13__4B(Input[14]), ._12__4A(Enable),
    ._11__4Y(Output[14]), ._10__3B(Input[15]), ._9__3A(Enable), ._8__3Y(Output[15]));
  _7486 u_7486_5 (
    ._1__1A(Input[16]), ._2__1B(Enable), ._3__1Y(Output[16]), ._4__2A(Input[17]), ._5__2B(Enable),
    ._6__2Y(Output[17]), ._7__GND(1'b0), ._14__Vcc(1'b1), ._13__4B(Input[18]), ._12__4A(Enable),
    ._11__4Y(Output[18]), ._10__3B(Input[19]), ._9__3A(Enable), ._8__3Y(Output[19]));
  _7486 u_7486_6 (
    ._1__1A(Input[20]), ._2__1B(Enable), ._3__1Y(Output[20]), ._4__2A(Input[21]), ._5__2B(Enable),
    ._6__2Y(Output[21]), ._7__GND(1'b0), ._14__Vcc(1'b1), ._13__4B(Input[22]), ._12__4A(Enable),
    ._11__4Y(Output[22]), ._10__3B(Input[23]), ._9__3A(Enable), ._8__3Y(Output[23]));
  _7486 u_7486_7 (
    ._1__1A(Input[24]), ._2__1B(Enable), ._3__1Y(Output[24]), ._4__2A(Input[25]), ._5__2B(Enable),
    ._6__2Y(Output[25]), ._7__GND(1'b0), ._14__Vcc(1'b1), ._13__4B(Input[26]), ._12__4A(Enable),
    ._11__4Y(Output[26]), ._10__3B(Input[27]), ._9__3A(Enable), ._8__3Y(Output[27]));
  _7486 u_7486_8 (
    ._1__1A(Input[28]), ._2__1B(Enable), ._3__1Y(Output[28]), ._4__2A(Input[29]), ._5__2B(Enable),
    ._6__2Y(Output[29]), ._7__GND(1'b0), ._14__Vcc(1'b1), ._13__4B(Input[30]), ._12__4A(Enable),
    ._11__4Y(Output[30]), ._10__3B(Input[31]), ._9__3A(Enable), ._8__3Y(Output[31]));
endmodule
