// Logisim project MantissaProcessingUnit.circ as structural Verilog: 4 circuits, main circuit main
module main (
);

  MPU mpu_1 ();  // open: Ea_Eb, ExpDiff, OutputSign, Cout, A, B, NormalizerInput

  // Notes on the sheet:
  //   Input : 32 bit fractions A and B (with sign,exponent and mantissa) , Ea < Eb and absolute exponent difference
  //   Output: Sign of final output, 32 bit normalizer input and carry out required for normalization
  //   MPU
endmodule

module MPU (
  input  [31:0] A,
  input  [31:0] B,
  input  Ea_Eb,
  input  [11:0] ExpDiff,
  output OutputSign,
  output Cout,
  output [31:0] NormalizerInput
);

  wire mantissacentralprocessor_1_enable2scomplement, mantissapreprocessor_1_largerexpsign,
       mantissapreprocessor_1_smallerexpsign;
  wire [19:0] mantissapreprocessor_1_largerexpmantissa, mantissapreprocessor_1_smallerexpmantissa;
  wire [31:0] mantissacentralprocessor_1_adder_output;

  MantissaPreprocessor mantissapreprocessor_1 (
    .Ea_Eb(Ea_Eb), .SmallerExpMantissa(mantissapreprocessor_1_smallerexpmantissa),
    .LargerExpMantissa(mantissapreprocessor_1_largerexpmantissa), .A(A), .B(B),
    .SmallerExpSign(mantissapreprocessor_1_smallerexpsign),
    .LargerExpSign(mantissapreprocessor_1_largerexpsign));
  MantissaCentralProcessor mantissacentralprocessor_1 (
    .ExpDiff(ExpDiff), .LargerExpSign(mantissapreprocessor_1_largerexpsign),
    .SmallerExpSign(mantissapreprocessor_1_smallerexpsign),
    .SmallerExpMantissa(mantissapreprocessor_1_smallerexpmantissa),
    .LargerExpMantissa(mantissapreprocessor_1_largerexpmantissa), .Sign_Y(OutputSign), .C_out(Cout),
    .Enable2sComplement(mantissacentralprocessor_1_enable2scomplement),
    .Adder_output(mantissacentralprocessor_1_adder_output));
  MantissaPostProcessor mantissapostprocessor_1 (
    .Enable2sComplement(mantissacentralprocessor_1_enable2scomplement), .NormalizerInput(NormalizerInput),
    .AdderOutput(mantissacentralprocessor_1_adder_output));

  // Other names for the same wires on the sheet: OS = OutputSign
endmodule

// ManPreProc
module MantissaPreprocessor (
  input  [31:0] A,
  input  [31:0] B,
  input  Ea_Eb,
  output [19:0] SmallerExpMantissa,
  output [19:0] LargerExpMantissa,
  output SmallerExpSign,
  output LargerExpSign
);

  wire [30:20] multiplexer_1_out, multiplexer_2_out;

  Multiplexer #(.width(32)) multiplexer_1 (
    .in0(B), .in1(A), .out({SmallerExpSign, multiplexer_1_out, SmallerExpMantissa}), .sel(Ea_Eb), .en(1'b1));
  Multiplexer #(.width(32)) multiplexer_2 (
    .in0(A), .in1(B), .out({LargerExpSign, multiplexer_2_out, LargerExpMantissa}), .sel(Ea_Eb), .en(1'b1));
endmodule

// ManPostProc
module MantissaPostProcessor (
  input  Enable2sComplement,
  input  [31:0] AdderOutput,
  output [31:0] NormalizerInput
);

  wire [31:0] n32bitinverterwithenable_1_output;

  _32BitInverterWithEnable u_32bitinverterwithenable_1 (
    .Enable(Enable2sComplement), .Input(AdderOutput), .Output(n32bitinverterwithenable_1_output));
  Adder #(.width(32)) adder_1 (
    .a(n32bitinverterwithenable_1_output), .b({32{1'b0}}), .out(NormalizerInput), .cin(Enable2sComplement));  // open: cout
endmodule
