// Logisim project RoundingUnit.circ as structural Verilog: 4 circuits, main circuit main
module main (
);

  RoundingUnit roundingunit_1 ();  // open: AdjustedExponent, RoundedMantissa, RoundingMantissa, RoundingExponent

  // Notes on the sheet:
  //   Output : 12 bit adjusted exponent and 20 bit rounded mantissa
  //   Input : 12 bit normalized exponent and 32 bit normalized mantissa
endmodule

// RU
module RoundingUnit (
  input  [11:0] RoundingExponent,
  input  [31:0] RoundingMantissa,
  output [11:0] AdjustedExponent,
  output [19:0] RoundedMantissa
);

  wire DecrementExp, roundupflag_1_roundup;
  wire [19:0] adder_1_out;

  // Probe on RoundingMantissa[31:12]
  RoundUpFlag roundupflag_1 (._20_32(RoundingMantissa[12:0]), .RoundUp(roundupflag_1_roundup));
  Adder #(.width(20)) adder_1 (
    .a(RoundingMantissa[31:12]), .b({20{1'b0}}), .out(adder_1_out), .cin(roundupflag_1_roundup),
    .cout(DecrementExp));
  // Probe on {4'b0000, DecrementExp}
  Shifter #(.width(20), .shift("lr")) shifter_1 (
    .in(adder_1_out), .\dist ({4'b0000, DecrementExp}), .out(RoundedMantissa));
  AdjustExponent adjustexponent_1 (
    .RoundingExponent(RoundingExponent), .AdjustedExponent(AdjustedExponent), .DecrementExp(DecrementExp));
endmodule

// RoundUp
module RoundUpFlag (
  input  [12:0] _20_32,
  output RoundUp
);

  wire n744075_1__6__2y, n744075_1__8__3y, n744075_1__12__1y, n744075_2__6__2y, n744075_2__8__3y,
       n744075_2__12__1y;

  _744075 u_744075_1 (
    ._1__1A(_20_32[9]), ._2__1B(_20_32[8]), ._3__2A(_20_32[4]), ._4__2B(_20_32[3]),
    ._5__2C(n744075_1__8__3y), ._6__2Y(n744075_1__6__2y), ._7__GND(1'b0), ._14__Vcc(1'b1),
    ._13__1C(_20_32[7]), ._12__1Y(n744075_1__12__1y), ._11__3C(n744075_1__12__1y), ._10__3B(_20_32[6]),
    ._9__3A(_20_32[5]), ._8__3Y(n744075_1__8__3y));
  _744075 u_744075_2 (
    ._1__1A(n744075_1__6__2y), ._2__1B(_20_32[2]), ._3__2A(1'b0), ._4__2B(_20_32[12]),
    ._5__2C(n744075_2__8__3y), ._6__2Y(n744075_2__6__2y), ._7__GND(1'b0), ._14__Vcc(1'b1),
    ._13__1C(_20_32[1]), ._12__1Y(n744075_2__12__1y), ._11__3C(n744075_2__12__1y), ._10__3B(_20_32[0]),
    ._9__3A(_20_32[10]), ._8__3Y(n744075_2__8__3y));
  _7408 u_7408_1 (
    ._1__1A(n744075_2__6__2y), ._2__1B(_20_32[11]), ._3__1Y(RoundUp), ._7__GND(1'b0), ._14__Vcc(1'b1));  // open: _4__2A, _5__2B, _6__2Y, _13__4B, _12__4A, _11__4Y, _10__3B, _9__3A, _8__3Y

  // Other names for the same wires on the sheet: _32 = _20_32[0]; _31 = _20_32[1]; _30 = _20_32[2]; _29 = _20_32[3];
  //   _28 = _20_32[4]; _27 = _20_32[5]; _26 = _20_32[6]; _25 = _20_32[7]; _24 = _20_32[8]; _23 = _20_32[9];
  //   R = _20_32[10]; G = _20_32[11]; _20 = _20_32[12]
endmodule

// AdjExp
module AdjustExponent (
  input  DecrementExp,
  input  [11:0] RoundingExponent,
  output [11:0] AdjustedExponent
);

  Subtractor #(.width(12)) subtractor_1 (
    .a(RoundingExponent), .b({12{1'b0}}), .out(AdjustedExponent), .bin(DecrementExp));  // open: bout
endmodule
