// Logisim project subtract_circuit.circ as structural Verilog: 1 circuit, main circuit main
// LS normalizer
module main (
  input  [11:0] Exponent_Input,
  input  [31:0] Input,
  output [11:0] LS_Norm_exponent,
  output LS_Norm_borrow,
  output [4:0] Shift_Amount,
  output [31:0] LS_Norm_mantissa,
  output All_Zeros
);

  wire bitfinder_1_found;

  BitFinder #(.width(32)) bitfinder_1 (
    .in({Input[0], Input[1], Input[2], Input[3], Input[4], Input[5], Input[6], Input[7], Input[8], Input[9], Input[10], Input[11], Input[12], Input[13], Input[14], Input[15], Input[16], Input[17], Input[18], Input[19], Input[20], Input[21], Input[22], Input[23], Input[24], Input[25], Input[26], Input[27], Input[28], Input[29], Input[30], Input[31]}),
    .index(Shift_Amount), .found(bitfinder_1_found));
  Shifter #(.width(32)) shifter_1 (.in(Input), .\dist (Shift_Amount), .out(LS_Norm_mantissa));
  Subtractor #(.width(12)) subtractor_1 (
    .a(Exponent_Input), .b({{7{1'b0}}, Shift_Amount}), .out(LS_Norm_exponent), .bout(LS_Norm_borrow));  // open: bin
  not not_1 (All_Zeros, bitfinder_1_found);
endmodule
