// Logisim project 32 bit right shift with empty.circ as structural Verilog: 1 circuit, main circuit main
module main (
  input  [11:0] in_1,
  input  [31:0] in_2,
  output [31:0] out_3
);

  wire n744075_1__6__2y, n744075_1__8__3y, n744075_1__12__1y;
  wire [31:0] shifter_1_out;

  _744075 u_744075_1 (
    ._1__1A(in_1[7]), ._2__1B(in_1[8]), ._3__2A(in_1[5]), ._4__2B(in_1[6]), ._5__2C(n744075_1__12__1y),
    ._6__2Y(n744075_1__6__2y), ._7__GND(1'b0), ._14__Vcc(1'b1), ._13__1C(n744075_1__8__3y),
    ._12__1Y(n744075_1__12__1y), ._11__3C(in_1[11]), ._10__3B(in_1[10]), ._9__3A(in_1[9]),
    ._8__3Y(n744075_1__8__3y));
  Shifter #(.width(32), .shift("lr")) shifter_1 (.in(in_2), .\dist (in_1[4:0]), .out(shifter_1_out));
  Multiplexer #(.width(32), .enable("false")) multiplexer_1 (
    .in0(shifter_1_out), .in1({32{1'b0}}), .out(out_3), .sel(n744075_1__6__2y));
endmodule
