// Logisim project Alu.circ as structural Verilog: 3 circuits, main circuit main
module main (
  input  [3:0] A,
  input  [3:0] B,
  input  [2:0] S,
  output [3:0] out_4,
  output Zero_Flag
);

  wire not_1_out, not_2_out, not_3_out, not_4_out, or_1_out, or_2_out;
  wire [3:0] multiplexer_1_out, multiplexer_2_out, n7408_1__3__1y, n7432_1__3__1y, n7483_1__9__s1,
       n7483_2__9__s1, nor_ic_1__3_1y, shifter_1_out, shifter_2_out;

  _7483 u_7483_1 (
    ._1__A4(A[3]), ._2__S3(n7483_1__9__s1[2]), ._3__A3(A[2]), ._4__B3(B[2]), ._5__Vcc(1'b1),
    ._6__S2(n7483_1__9__s1[1]), ._7__B2(B[1]), ._8__A2(A[1]), ._16__B4(B[3]), ._15__S4(n7483_1__9__s1[3]),
    ._13__Cin(1'b0), ._12__GND(1'b0), ._11__B1(B[0]), ._10__A1(A[0]), ._9__S1(n7483_1__9__s1[0]));  // open: _14__Cout
  not not_1 (not_1_out, B[0]);
  not not_2 (not_2_out, B[3]);
  or or_1 (or_1_out, B[2], B[3]);
  or or_2 (or_2_out, B[2], B[3]);
  _7432 u_7432_1 (
    ._1__1A(A[0]), ._2__1B(B[0]), ._3__1Y(n7432_1__3__1y[0]), ._4__2A(A[1]), ._5__2B(B[1]),
    ._6__2Y(n7432_1__3__1y[1]), ._7__GND(1'b0), ._14__Vcc(1'b1), ._13__4B(B[3]), ._12__4A(A[3]),
    ._11__4Y(n7432_1__3__1y[3]), ._10__3B(B[2]), ._9__3A(A[2]), ._8__3Y(n7432_1__3__1y[2]));
  _7408 u_7408_1 (
    ._1__1A(A[0]), ._2__1B(B[0]), ._3__1Y(n7408_1__3__1y[0]), ._4__2A(A[1]), ._5__2B(B[1]),
    ._6__2Y(n7408_1__3__1y[1]), ._7__GND(1'b0), ._14__Vcc(1'b1), ._13__4B(B[3]), ._12__4A(A[3]),
    ._11__4Y(n7408_1__3__1y[3]), ._10__3B(B[2]), ._9__3A(A[2]), ._8__3Y(n7408_1__3__1y[2]));
  NOr_IC nor_ic_1 (
    ._14_VCC(1'b1), ._1_1A(A[0]), ._2_1B(B[0]), ._13_4B(B[3]), ._3_1Y(nor_ic_1__3_1y[0]), ._4_2A(A[1]),
    ._5_2B(B[1]), ._6_2Y(nor_ic_1__3_1y[1]), ._7_GND(1'b0), ._12_4A(A[3]), ._11_4Y(nor_ic_1__3_1y[3]),
    ._10_3B(B[2]), ._9_3A(A[2]), ._8_3Y(nor_ic_1__3_1y[2]));
  _7483 u_7483_2 (
    ._1__A4(A[3]), ._2__S3(n7483_2__9__s1[2]), ._3__A3(A[2]), ._4__B3(not_4_out), ._5__Vcc(1'b1),
    ._6__S2(n7483_2__9__s1[1]), ._7__B2(not_3_out), ._8__A2(A[1]), ._16__B4(not_2_out),
    ._15__S4(n7483_2__9__s1[3]), ._13__Cin(1'b1), ._12__GND(1'b0), ._11__B1(not_1_out), ._10__A1(A[0]),
    ._9__S1(n7483_2__9__s1[0]));  // open: _14__Cout
  not not_3 (not_3_out, B[1]);
  not not_4 (not_4_out, B[2]);
  Shifter #(.width(4)) shifter_1 (.in(A), .\dist (B[1:0]), .out(shifter_1_out));
  Shifter #(.width(4), .shift("lr")) shifter_2 (.in(A), .\dist (B[1:0]), .out(shifter_2_out));
  Multiplexer #(.width(4)) multiplexer_1 (
    .in0(shifter_1_out), .in1(4'b0000), .out(multiplexer_1_out), .sel(or_1_out), .en(1'b1));
  Multiplexer #(.width(4)) multiplexer_2 (
    .in0(shifter_2_out), .in1(4'b0000), .out(multiplexer_2_out), .sel(or_2_out), .en(1'b1));
  Multiplexer #(.select(3), .width(4)) multiplexer_3 (
    .in0(n7483_1__9__s1), .in1(n7483_2__9__s1), .in2(n7432_1__3__1y), .in3(n7408_1__3__1y),
    .in4(nor_ic_1__3_1y), .in5(multiplexer_1_out), .in6(multiplexer_2_out), .in7(4'b0000), .out(out_4),
    .sel(S));  // open: en
  nor nor_1 (Zero_Flag, out_4[0], out_4[1], out_4[2], out_4[3]);
endmodule

// NOR_IC
module NOr_IC (
  input  _14_VCC,
  input  _1_1A,
  input  _12_4A,
  input  _2_1B,
  input  _13_4B,
  input  _10_3B,
  input  _9_3A,
  input  _4_2A,
  input  _5_2B,
  input  _7_GND,
  output _11_4Y,
  output _3_1Y,
  output _6_2Y,
  output _8_3Y
);

  nor nor_1 (_3_1Y, _2_1B, _1_1A);
  nor nor_2 (_6_2Y, _5_2B, _4_2A);
  nor nor_3 (_11_4Y, _13_4B, _12_4A);
  nor nor_4 (_8_3Y, _10_3B, _9_3A);
endmodule

module test (
  input  [3:0] A,
  input  [3:0] B,
  input  [2:0] ALUop,
  output [3:0] Result,
  output Zero
);

  main main_1 (.A(A), .B(B), .S(ALUop), .out_4(Result), .Zero_Flag(Zero));
endmodule
