// Logisim project Control Unit.circ as structural Verilog: 2 circuits, main circuit main
module main (
);

  Control_Unit control_unit_1 ();  // open: Opcode, ALUOp, Branch, Jump, Bneq, MemtoReg, MemRead, MemWrite, RegWrite, RegDst, ALUSrc
endmodule

// Control
module Control_Unit (
  input  [3:0] Opcode,
  output [2:0] ALUOp,
  output Branch,
  output Jump,
  output Bneq,
  output MemtoReg,
  output MemRead,
  output MemWrite,
  output RegWrite,
  output RegDst,
  output ALUSrc
);

  ROM #(.addrWidth(4), .dataWidth(12)) rom_1 (
    .addr(Opcode), .data({ALUOp, Branch, Jump, Bneq, MemtoReg, MemRead, MemWrite, RegWrite, RegDst, ALUSrc}),
    .sel(1'b1));

  // Notes on the sheet:
  //   contents of rom_1 (hex, n*v repeats v):
  //   606 605 300 e80 340 206 205 5 a05 406 6 405 35 c05 806 9
endmodule
