// Logisim project DataMemory.circ as structural Verilog: 2 circuits, main circuit DataMemory
module DataMemory (
  input  [3:0] ALUOutput,
  input  [3:0] RegData,
  input  MemWrite,
  input  MemRead,
  input  MemToReg,
  input  Clock,
  output [3:0] DataToWrite
);

  wire [3:0] ram_1_data;

  RAM #(.addrWidth(4), .dataWidth(4), .bus("separate")) ram_1 (
    .addr(ALUOutput), .din(RegData), .data(ram_1_data), .str(MemWrite), .sel(1'b1), .clk(Clock), .ld(MemRead));  // open: clr
  Multiplexer #(.width(4)) multiplexer_1 (
    .in0(ALUOutput), .in1(ram_1_data), .out(DataToWrite), .sel(MemToReg), .en(1'b1));
endmodule

// DataMemory
module Main (
);

  DataMemory DataMemory ();  // open: ALUOutput, RegData, MemWrite, Clock, MemRead, MemToReg, DataToWrite
endmodule
