// Logisim project RegisterFile4.circ as structural Verilog: 2 circuits, main circuit main
// Register File
module main (
  input  [3:0] ReadReg1,
  input  [3:0] ReadReg2,
  input  [3:0] WriteData,
  input  [3:0] WriteReg,
  input  RegWriteEnable,
  input  Clock,
  output [3:0] RegData1,
  output [3:0] RegData2,
  output [3:0] t0,
  output [3:0] t1,
  output [3:0] t2,
  output [3:0] t3,
  output [3:0] t4,
  output [3:0] t5,
  output [3:0] sp
);

  wire n7404_1__2__1y, n7404_1__4__2y, n7404_1__6__3y, n7404_1__8__4y, n7404_1__10__5y, n7404_1__12__6y,
       n7404_2__2__1y, n7404_2__4__2y, n7404_2__6__3y, n7404_2__8__4y, n7404_2__10__5y, n7404_2__12__6y,
       n7404_3__2__1y, n7404_3__4__2y, n7408_1__3__1y, n7408_1__6__2y, n7408_1__11__4y, n7408_2__3__1y,
       n7408_2__6__2y, n7408_2__8__3y, n7408_2__11__4y, n7408_3__3__1y, n7408_3__6__2y, n7408_3__8__3y,
       n7408_3__11__4y, n7408_4__3__1y, n7408_4__6__2y, n7408_4__8__3y, n7408_4__11__4y, n7408_5__3__1y,
       n7408_5__6__2y, n7408_5__8__3y, n7408_5__11__4y, n7408_6__3__1y, n7408_6__6__2y, n7408_6__8__3y,
       n7408_6__11__4y, n7408_7__3__1y, n7408_7__6__2y, n7408_7__8__3y, n7408_7__11__4y, n7408_8__3__1y,
       n7408_8__6__2y, n7408_8__8__3y, n7408_8__11__4y, n7408_9__3__1y, n7408_9__6__2y, n7408_9__8__3y,
       n7408_9__11__4y, n7408_10__3__1y, n7408_10__6__2y, n7408_10__8__3y, n7408_10__11__4y, n7408_11__3__1y,
       n7408_11__6__2y, n7408_11__8__3y, n7408_11__11__4y, n7408_12__3__1y, n7408_12__6__2y, n7408_12__8__3y,
       n7408_12__11__4y, n7408_13__3__1y, n7408_13__6__2y, n7408_13__8__3y, n7408_13__11__4y,
       n7408_14__3__1y, n7408_14__6__2y, n7408_14__8__3y, n7408_14__11__4y, n7408_15__3__1y, n7408_15__6__2y,
       n7408_15__8__3y, n7408_15__11__4y, n7408_16__3__1y, n7408_16__6__2y, n7408_16__8__3y,
       n7408_16__11__4y, n74138_1__7__y7, n74138_1__9__y6, n74138_1__10__y5, n74138_1__11__y4,
       n74138_1__12__y3, n74138_1__13__y2, n74138_1__14__y1, n74153_1__7__y1, n74153_1__9__y2,
       n74153_2__7__y1, n74153_2__9__y2, n74153_3__7__y1, n74153_3__9__y2, n74153_4__7__y1, n74153_4__9__y2,
       n74153_5__7__y1, n74153_5__9__y2, n74153_6__7__y1, n74153_6__9__y2, n74153_7__7__y1, n74153_7__9__y2,
       n74153_8__7__y1, n74153_8__9__y2;
  wire [3:0] n7432_1__3__1y, n7432_2__3__1y, n7432_3__3__1y, n7432_4__3__1y, n7432_5__3__1y, n7432_6__3__1y,
       n7432_7__3__1y;

  _74138 u_74138_1 (
    ._1__A(WriteReg[0]), ._2__B(WriteReg[1]), ._3__C(WriteReg[2]), ._4__G2A(1'b0), ._5__G2B(1'b0),
    ._6__G1(1'b1), ._7__Y7(n74138_1__7__y7), ._8__GND(1'b0), ._16__Vcc(1'b1), ._14__Y1(n74138_1__14__y1),
    ._13__Y2(n74138_1__13__y2), ._12__Y3(n74138_1__12__y3), ._11__Y4(n74138_1__11__y4),
    ._10__Y5(n74138_1__10__y5), ._9__Y6(n74138_1__9__y6));  // open: _15__Y0
  _7404 u_7404_1 (
    ._1__1A(n74138_1__14__y1), ._2__1Y(n7404_1__2__1y), ._3__2A(n74138_1__13__y2), ._4__2Y(n7404_1__4__2y),
    ._5__3A(n74138_1__12__y3), ._6__3Y(n7404_1__6__3y), ._7__GND(1'b0), ._14__Vcc(1'b1),
    ._13__6A(n74138_1__11__y4), ._12__6Y(n7404_1__12__6y), ._11__5A(n74138_1__10__y5),
    ._10__5Y(n7404_1__10__5y), ._9__4A(n74138_1__9__y6), ._8__4Y(n7404_1__8__4y));
  _7404 u_7404_2 (
    ._1__1A(n74138_1__7__y7), ._2__1Y(n7404_2__2__1y), ._3__2A(n7408_2__3__1y), ._4__2Y(n7404_2__4__2y),
    ._5__3A(n7408_2__6__2y), ._6__3Y(n7404_2__6__3y), ._7__GND(1'b0), ._14__Vcc(1'b1),
    ._13__6A(n7408_2__11__4y), ._12__6Y(n7404_2__12__6y), ._11__5A(n7408_2__8__3y),
    ._10__5Y(n7404_2__10__5y), ._9__4A(n7408_1__3__1y), ._8__4Y(n7404_2__8__4y));
  _7408 u_7408_1 (
    ._1__1A(RegWriteEnable), ._2__1B(n7404_1__10__5y), ._3__1Y(n7408_1__3__1y), ._4__2A(n7404_1__8__4y),
    ._5__2B(RegWriteEnable), ._6__2Y(n7408_1__6__2y), ._7__GND(1'b0), ._14__Vcc(1'b0),
    ._13__4B(RegWriteEnable), ._12__4A(n7404_2__2__1y), ._11__4Y(n7408_1__11__4y));  // open: _10__3B, _9__3A, _8__3Y
  _7408 u_7408_2 (
    ._1__1A(RegWriteEnable), ._2__1B(n7404_1__2__1y), ._3__1Y(n7408_2__3__1y), ._4__2A(RegWriteEnable),
    ._5__2B(n7404_1__4__2y), ._6__2Y(n7408_2__6__2y), ._7__GND(1'b0), ._14__Vcc(1'b0),
    ._13__4B(RegWriteEnable), ._12__4A(n7404_1__6__3y), ._11__4Y(n7408_2__11__4y), ._10__3B(RegWriteEnable),
    ._9__3A(n7404_1__12__6y), ._8__3Y(n7408_2__8__3y));
  _7404 u_7404_3 (
    ._1__1A(n7408_1__6__2y), ._2__1Y(n7404_3__2__1y), ._3__2A(n7408_1__11__4y), ._4__2Y(n7404_3__4__2y),
    ._7__GND(1'b0), ._14__Vcc(1'b1));  // open: _5__3A, _6__3Y, _13__6A, _12__6Y, _11__5A, _10__5Y, _9__4A, _8__4Y
  _7408 u_7408_3 (
    ._1__1A(WriteData[0]), ._2__1B(n7408_2__3__1y), ._3__1Y(n7408_3__3__1y), ._4__2A(WriteData[1]),
    ._5__2B(n7408_2__3__1y), ._6__2Y(n7408_3__6__2y), ._7__GND(1'b0), ._14__Vcc(1'b1),
    ._13__4B(WriteData[2]), ._12__4A(n7408_2__3__1y), ._11__4Y(n7408_3__11__4y), ._10__3B(WriteData[3]),
    ._9__3A(n7408_2__3__1y), ._8__3Y(n7408_3__8__3y));
  _7432 u_7432_1 (
    ._1__1A(n7408_3__3__1y), ._2__1B(n7408_4__3__1y), ._3__1Y(n7432_1__3__1y[0]), ._4__2A(n7408_3__6__2y),
    ._5__2B(n7408_4__6__2y), ._6__2Y(n7432_1__3__1y[1]), ._7__GND(1'b0), ._14__Vcc(1'b1),
    ._13__4B(n7408_3__11__4y), ._12__4A(n7408_4__11__4y), ._11__4Y(n7432_1__3__1y[2]),
    ._10__3B(n7408_3__8__3y), ._9__3A(n7408_4__8__3y), ._8__3Y(n7432_1__3__1y[3]));
  _7408 u_7408_4 (
    ._1__1A(n7404_2__4__2y), ._2__1B(t0[0]), ._3__1Y(n7408_4__3__1y), ._4__2A(n7404_2__4__2y),
    ._5__2B(t0[1]), ._6__2Y(n7408_4__6__2y), ._7__GND(1'b0), ._14__Vcc(1'b1), ._13__4B(n7404_2__4__2y),
    ._12__4A(t0[2]), ._11__4Y(n7408_4__11__4y), ._10__3B(n7404_2__4__2y), ._9__3A(t0[3]),
    ._8__3Y(n7408_4__8__3y));
  Register #(.width(4)) u_t0 (.D(n7432_1__3__1y), .Q(t0), .clk(Clock));  // open: en, clr
  _7408 u_7408_5 (
    ._1__1A(n7408_2__6__2y), ._2__1B(WriteData[0]), ._3__1Y(n7408_5__3__1y), ._4__2A(n7408_2__6__2y),
    ._5__2B(WriteData[1]), ._6__2Y(n7408_5__6__2y), ._7__GND(1'b0), ._14__Vcc(1'b1),
    ._13__4B(n7408_2__6__2y), ._12__4A(WriteData[2]), ._11__4Y(n7408_5__11__4y), ._10__3B(n7408_2__6__2y),
    ._9__3A(WriteData[3]), ._8__3Y(n7408_5__8__3y));
  _7432 u_7432_2 (
    ._1__1A(n7408_5__3__1y), ._2__1B(n7408_6__3__1y), ._3__1Y(n7432_2__3__1y[0]), ._4__2A(n7408_5__6__2y),
    ._5__2B(n7408_6__6__2y), ._6__2Y(n7432_2__3__1y[1]), ._7__GND(1'b0), ._14__Vcc(1'b1),
    ._13__4B(n7408_5__11__4y), ._12__4A(n7408_6__11__4y), ._11__4Y(n7432_2__3__1y[2]),
    ._10__3B(n7408_5__8__3y), ._9__3A(n7408_6__8__3y), ._8__3Y(n7432_2__3__1y[3]));
  _7408 u_7408_6 (
    ._1__1A(n7404_2__6__3y), ._2__1B(t1[0]), ._3__1Y(n7408_6__3__1y), ._4__2A(n7404_2__6__3y),
    ._5__2B(t1[1]), ._6__2Y(n7408_6__6__2y), ._7__GND(1'b0), ._14__Vcc(1'b1), ._13__4B(n7404_2__6__3y),
    ._12__4A(t1[2]), ._11__4Y(n7408_6__11__4y), ._10__3B(n7404_2__6__3y), ._9__3A(t1[3]),
    ._8__3Y(n7408_6__8__3y));
  Register #(.width(4)) u_t1 (.D(n7432_2__3__1y), .Q(t1), .clk(Clock));  // open: en, clr
  _7408 u_7408_7 (
    ._1__1A(n7408_2__11__4y), ._2__1B(WriteData[0]), ._3__1Y(n7408_7__3__1y), ._4__2A(n7408_2__11__4y),
    ._5__2B(WriteData[1]), ._6__2Y(n7408_7__6__2y), ._7__GND(1'b0), ._14__Vcc(1'b1),
    ._13__4B(n7408_2__11__4y), ._12__4A(WriteData[2]), ._11__4Y(n7408_7__11__4y), ._10__3B(n7408_2__11__4y),
    ._9__3A(WriteData[3]), ._8__3Y(n7408_7__8__3y));
  _7432 u_7432_3 (
    ._1__1A(n7408_7__3__1y), ._2__1B(n7408_8__3__1y), ._3__1Y(n7432_3__3__1y[0]), ._4__2A(n7408_7__6__2y),
    ._5__2B(n7408_8__6__2y), ._6__2Y(n7432_3__3__1y[1]), ._7__GND(1'b0), ._14__Vcc(1'b1),
    ._13__4B(n7408_7__11__4y), ._12__4A(n7408_8__11__4y), ._11__4Y(n7432_3__3__1y[2]),
    ._10__3B(n7408_7__8__3y), ._9__3A(n7408_8__8__3y), ._8__3Y(n7432_3__3__1y[3]));
  _7408 u_7408_8 (
    ._1__1A(n7404_2__12__6y), ._2__1B(t2[0]), ._3__1Y(n7408_8__3__1y), ._4__2A(n7404_2__12__6y),
    ._5__2B(t2[1]), ._6__2Y(n7408_8__6__2y), ._7__GND(1'b0), ._14__Vcc(1'b1), ._13__4B(n7404_2__12__6y),
    ._12__4A(t2[2]), ._11__4Y(n7408_8__11__4y), ._10__3B(n7404_2__12__6y), ._9__3A(t2[3]),
    ._8__3Y(n7408_8__8__3y));
  Register #(.width(4)) u_t2 (.D(n7432_3__3__1y), .Q(t2), .clk(Clock));  // open: en, clr
  _74153 u_74153_1 (
    ._1__nG1(1'b0), ._2__B(ReadReg1[1]), ._3__1C3(t2[0]), ._4__1C2(t1[0]), ._5__1C1(t0[0]), ._6__1C0(1'b0),
    ._7__Y1(n74153_1__7__y1), ._8__GND(1'b0), ._16__Vcc(1'b1), ._15__nG2(1'b0), ._14__A(ReadReg1[0]),
    ._13__2C3(t2[1]), ._12__2C2(t1[1]), ._11__2C1(t0[1]), ._10__2C0(1'b0), ._9__Y2(n74153_1__9__y2));
  _74153 u_74153_2 (
    ._1__nG1(1'b0), ._2__B(ReadReg2[1]), ._3__1C3(t2[0]), ._4__1C2(t1[0]), ._5__1C1(t0[0]), ._6__1C0(1'b0),
    ._7__Y1(n74153_2__7__y1), ._8__GND(1'b0), ._16__Vcc(1'b1), ._15__nG2(1'b0), ._14__A(ReadReg2[0]),
    ._13__2C3(t2[1]), ._12__2C2(t1[1]), ._11__2C1(t0[1]), ._10__2C0(1'b0), ._9__Y2(n74153_2__9__y2));
  _7408 u_7408_9 (
    ._1__1A(n7408_2__8__3y), ._2__1B(WriteData[0]), ._3__1Y(n7408_9__3__1y), ._4__2A(n7408_2__8__3y),
    ._5__2B(WriteData[1]), ._6__2Y(n7408_9__6__2y), ._7__GND(1'b0), ._14__Vcc(1'b1),
    ._13__4B(n7408_2__8__3y), ._12__4A(WriteData[2]), ._11__4Y(n7408_9__11__4y), ._10__3B(n7408_2__8__3y),
    ._9__3A(WriteData[3]), ._8__3Y(n7408_9__8__3y));
  _7432 u_7432_4 (
    ._1__1A(n7408_9__3__1y), ._2__1B(n7408_10__3__1y), ._3__1Y(n7432_4__3__1y[0]), ._4__2A(n7408_9__6__2y),
    ._5__2B(n7408_10__6__2y), ._6__2Y(n7432_4__3__1y[1]), ._7__GND(1'b0), ._14__Vcc(1'b1),
    ._13__4B(n7408_9__11__4y), ._12__4A(n7408_10__11__4y), ._11__4Y(n7432_4__3__1y[2]),
    ._10__3B(n7408_9__8__3y), ._9__3A(n7408_10__8__3y), ._8__3Y(n7432_4__3__1y[3]));
  _7408 u_7408_10 (
    ._1__1A(n7404_2__10__5y), ._2__1B(t3[0]), ._3__1Y(n7408_10__3__1y), ._4__2A(n7404_2__10__5y),
    ._5__2B(t3[1]), ._6__2Y(n7408_10__6__2y), ._7__GND(1'b0), ._14__Vcc(1'b1), ._13__4B(n7404_2__10__5y),
    ._12__4A(t3[2]), ._11__4Y(n7408_10__11__4y), ._10__3B(n7404_2__10__5y), ._9__3A(t3[3]),
    ._8__3Y(n7408_10__8__3y));
  _74153 u_74153_3 (
    ._1__nG1(1'b0), ._2__B(ReadReg1[1]), ._3__1C3(t2[2]), ._4__1C2(t1[2]), ._5__1C1(t0[2]), ._6__1C0(1'b0),
    ._7__Y1(n74153_3__7__y1), ._8__GND(1'b0), ._16__Vcc(1'b1), ._15__nG2(1'b0), ._14__A(ReadReg1[0]),
    ._13__2C3(t2[3]), ._12__2C2(t1[3]), ._11__2C1(t0[3]), ._10__2C0(1'b0), ._9__Y2(n74153_3__9__y2));
  _74153 u_74153_4 (
    ._1__nG1(1'b0), ._2__B(ReadReg2[1]), ._3__1C3(t2[2]), ._4__1C2(t1[2]), ._5__1C1(t0[2]), ._6__1C0(1'b0),
    ._7__Y1(n74153_4__7__y1), ._8__GND(1'b0), ._16__Vcc(1'b1), ._15__nG2(1'b0), ._14__A(ReadReg2[0]),
    ._13__2C3(t2[3]), ._12__2C2(t1[3]), ._11__2C1(t0[3]), ._10__2C0(1'b0), ._9__Y2(n74153_4__9__y2));
  Register #(.width(4)) u_t3 (.D(n7432_4__3__1y), .Q(t3), .clk(Clock));  // open: en, clr
  _7408 u_7408_11 (
    ._1__1A(n7408_1__3__1y), ._2__1B(WriteData[0]), ._3__1Y(n7408_11__3__1y), ._4__2A(n7408_1__3__1y),
    ._5__2B(WriteData[1]), ._6__2Y(n7408_11__6__2y), ._7__GND(1'b0), ._14__Vcc(1'b1), ._13__4B(WriteData[2]),
    ._12__4A(n7408_1__3__1y), ._11__4Y(n7408_11__11__4y), ._10__3B(n7408_1__3__1y), ._9__3A(WriteData[3]),
    ._8__3Y(n7408_11__8__3y));
  _7432 u_7432_5 (
    ._1__1A(n7408_11__3__1y), ._2__1B(n7408_12__3__1y), ._3__1Y(n7432_5__3__1y[0]), ._4__2A(n7408_11__6__2y),
    ._5__2B(n7408_12__6__2y), ._6__2Y(n7432_5__3__1y[1]), ._7__GND(1'b0), ._14__Vcc(1'b1),
    ._13__4B(n7408_11__11__4y), ._12__4A(n7408_12__11__4y), ._11__4Y(n7432_5__3__1y[2]),
    ._10__3B(n7408_11__8__3y), ._9__3A(n7408_12__8__3y), ._8__3Y(n7432_5__3__1y[3]));
  _7408 u_7408_12 (
    ._1__1A(n7404_2__8__4y), ._2__1B(t4[0]), ._3__1Y(n7408_12__3__1y), ._4__2A(n7404_2__8__4y),
    ._5__2B(t4[1]), ._6__2Y(n7408_12__6__2y), ._7__GND(1'b0), ._14__Vcc(1'b1), ._13__4B(n7404_2__8__4y),
    ._12__4A(t4[2]), ._11__4Y(n7408_12__11__4y), ._10__3B(n7404_2__8__4y), ._9__3A(t4[3]),
    ._8__3Y(n7408_12__8__3y));
  _74157 u_74157_1 (
    ._1__S(ReadReg2[2]), ._2__A1(n74153_2__7__y1), ._3__B1(n74153_6__7__y1), ._4__Y1(RegData2[0]),
    ._5__A2(n74153_2__9__y2), ._6__B2(n74153_6__9__y2), ._7__Y2(RegData2[1]), ._8__GND(1'b0),
    ._16__Vcc(1'b1), ._15__G(1'b0), ._14__A4(n74153_4__7__y1), ._13__B4(n74153_8__7__y1),
    ._12__Y4(RegData2[2]), ._11__A3(n74153_4__9__y2), ._10__B3(n74153_8__9__y2), ._9__Y3(RegData2[3]));
  Register #(.width(4)) u_t4 (.D(n7432_5__3__1y), .Q(t4), .clk(Clock));  // open: en, clr
  _7408 u_7408_13 (
    ._1__1A(n7408_1__6__2y), ._2__1B(WriteData[0]), ._3__1Y(n7408_13__3__1y), ._4__2A(n7408_1__6__2y),
    ._5__2B(WriteData[1]), ._6__2Y(n7408_13__6__2y), ._7__GND(1'b0), ._14__Vcc(1'b1),
    ._13__4B(n7408_1__6__2y), ._12__4A(WriteData[2]), ._11__4Y(n7408_13__11__4y), ._10__3B(n7408_1__6__2y),
    ._9__3A(WriteData[3]), ._8__3Y(n7408_13__8__3y));
  _7432 u_7432_6 (
    ._1__1A(n7408_13__3__1y), ._2__1B(n7408_14__3__1y), ._3__1Y(n7432_6__3__1y[0]), ._4__2A(n7408_13__6__2y),
    ._5__2B(n7408_14__6__2y), ._6__2Y(n7432_6__3__1y[1]), ._7__GND(1'b0), ._14__Vcc(1'b1),
    ._13__4B(n7408_13__11__4y), ._12__4A(n7408_14__11__4y), ._11__4Y(n7432_6__3__1y[2]),
    ._10__3B(n7408_13__8__3y), ._9__3A(n7408_14__8__3y), ._8__3Y(n7432_6__3__1y[3]));
  _7408 u_7408_14 (
    ._1__1A(n7404_3__2__1y), ._2__1B(t5[0]), ._3__1Y(n7408_14__3__1y), ._4__2A(n7404_3__2__1y),
    ._5__2B(t5[1]), ._6__2Y(n7408_14__6__2y), ._7__GND(1'b0), ._14__Vcc(1'b1), ._13__4B(n7404_3__2__1y),
    ._12__4A(t5[2]), ._11__4Y(n7408_14__11__4y), ._10__3B(n7404_3__2__1y), ._9__3A(t5[3]),
    ._8__3Y(n7408_14__8__3y));
  _74157 u_74157_2 (
    ._1__S(ReadReg1[2]), ._2__A1(n74153_1__7__y1), ._3__B1(n74153_5__7__y1), ._4__Y1(RegData1[0]),
    ._5__A2(n74153_1__9__y2), ._6__B2(n74153_5__9__y2), ._7__Y2(RegData1[1]), ._8__GND(1'b0),
    ._16__Vcc(1'b1), ._15__G(1'b0), ._14__A4(n74153_3__7__y1), ._13__B4(n74153_7__7__y1),
    ._12__Y4(RegData1[2]), ._11__A3(n74153_3__9__y2), ._10__B3(n74153_7__9__y2), ._9__Y3(RegData1[3]));
  Register #(.width(4)) u_t5 (.D(n7432_6__3__1y), .Q(t5), .clk(Clock));  // open: en, clr
  _7408 u_7408_15 (
    ._1__1A(n7408_1__11__4y), ._2__1B(WriteData[0]), ._3__1Y(n7408_15__3__1y), ._4__2A(n7408_1__11__4y),
    ._5__2B(WriteData[1]), ._6__2Y(n7408_15__6__2y), ._7__GND(1'b0), ._14__Vcc(1'b1),
    ._13__4B(n7408_1__11__4y), ._12__4A(WriteData[2]), ._11__4Y(n7408_15__11__4y), ._10__3B(n7408_1__11__4y),
    ._9__3A(WriteData[3]), ._8__3Y(n7408_15__8__3y));
  _7432 u_7432_7 (
    ._1__1A(n7408_15__3__1y), ._2__1B(n7408_16__3__1y), ._3__1Y(n7432_7__3__1y[0]), ._4__2A(n7408_15__6__2y),
    ._5__2B(n7408_16__6__2y), ._6__2Y(n7432_7__3__1y[1]), ._7__GND(1'b0), ._14__Vcc(1'b1),
    ._13__4B(n7408_15__11__4y), ._12__4A(n7408_16__11__4y), ._11__4Y(n7432_7__3__1y[2]),
    ._10__3B(n7408_15__8__3y), ._9__3A(n7408_16__8__3y), ._8__3Y(n7432_7__3__1y[3]));
  _7408 u_7408_16 (
    ._1__1A(n7404_3__4__2y), ._2__1B(sp[0]), ._3__1Y(n7408_16__3__1y), ._4__2A(n7404_3__4__2y),
    ._5__2B(sp[1]), ._6__2Y(n7408_16__6__2y), ._7__GND(1'b0), ._14__Vcc(1'b1), ._13__4B(n7404_3__4__2y),
    ._12__4A(sp[2]), ._11__4Y(n7408_16__11__4y), ._10__3B(n7404_3__4__2y), ._9__3A(sp[3]),
    ._8__3Y(n7408_16__8__3y));
  Register #(.width(4)) u_sp (.D(n7432_7__3__1y), .Q(sp), .clk(Clock));  // open: en, clr
  _74153 u_74153_5 (
    ._1__nG1(1'b0), ._2__B(ReadReg1[1]), ._3__1C3(sp[0]), ._4__1C2(t5[0]), ._5__1C1(t4[0]), ._6__1C0(t3[0]),
    ._7__Y1(n74153_5__7__y1), ._8__GND(1'b0), ._16__Vcc(1'b1), ._15__nG2(1'b0), ._14__A(ReadReg1[0]),
    ._13__2C3(sp[1]), ._12__2C2(t5[1]), ._11__2C1(t4[1]), ._10__2C0(t3[1]), ._9__Y2(n74153_5__9__y2));
  _74153 u_74153_6 (
    ._1__nG1(1'b0), ._2__B(ReadReg2[1]), ._3__1C3(sp[0]), ._4__1C2(t5[0]), ._5__1C1(t4[0]), ._6__1C0(t3[0]),
    ._7__Y1(n74153_6__7__y1), ._8__GND(1'b0), ._16__Vcc(1'b1), ._15__nG2(1'b0), ._14__A(ReadReg2[0]),
    ._13__2C3(sp[1]), ._12__2C2(t5[1]), ._11__2C1(t4[1]), ._10__2C0(t3[1]), ._9__Y2(n74153_6__9__y2));
  _74153 u_74153_7 (
    ._1__nG1(1'b0), ._2__B(ReadReg1[1]), ._3__1C3(sp[2]), ._4__1C2(t5[2]), ._5__1C1(t4[2]), ._6__1C0(t3[2]),
    ._7__Y1(n74153_7__7__y1), ._8__GND(1'b0), ._16__Vcc(1'b1), ._15__nG2(1'b0), ._14__A(ReadReg1[0]),
    ._13__2C3(sp[3]), ._12__2C2(t5[3]), ._11__2C1(t4[3]), ._10__2C0(t3[3]), ._9__Y2(n74153_7__9__y2));
  _74153 u_74153_8 (
    ._1__nG1(1'b0), ._2__B(ReadReg2[1]), ._3__1C3(sp[2]), ._4__1C2(t5[2]), ._5__1C1(t4[2]), ._6__1C0(t3[2]),
    ._7__Y1(n74153_8__7__y1), ._8__GND(1'b0), ._16__Vcc(1'b1), ._15__nG2(1'b0), ._14__A(ReadReg2[0]),
    ._13__2C3(sp[3]), ._12__2C2(t5[3]), ._11__2C1(t4[3]), ._10__2C0(t3[3]), ._9__Y2(n74153_8__9__y2));
endmodule

module test (
);

  main main_1 ();  // open: ReadReg1, ReadReg2, WriteData, WriteReg, RegWriteEnable, Clock, RegData1, RegData2, t0, t1, t2, t3, t4, t5, sp
endmodule
